// Digital circuit Address_Decode.dig as structural Verilog
module Address_Decode (
  input  A0,
  input  A1,
  input  A2,
  input  A3,
  input  A4,
  input  A5,
  input  A6,
  input  A7,
  input  A8,
  input  A9,
  input  A10,
  input  R_nW,
  input  AS,
  input  A11,
  input  A12,
  input  A13,
  output nQ3,
  output nQ0,
  output nQ1,
  output nQ2,
  output nQ4,
  output nQ5,
  output nQ6,
  output nQ7,
  output nQ0_2,
  output nQ1_2,
  output nQ2_2,
  output nQ3_2,
  output nQ4_2,
  output nQ5_2,
  output nQ6_2,
  output nQ7_2,
  output nQ0_3,
  output nQ1_3,
  output nQ2_3,
  output nQ3_3,
  output nQ4_3,
  output nQ5_3,
  output nQ6_3,
  output nQ7_3,
  output ACIA_CS0,
  output RTC_CS1,
  output RAM1_nCS,
  output RAM2_nCS,
  output ROM_nCE,
  output ACIA_CS1,
  output ACIA_nCS2,
  output ACIA_R_nW,
  output ACIA_E,
  output ACIA_RS,
  output RTC_CS2,
  output RTC_ADDRESS_WRITE,
  output RTC_READ,
  output RTC_WRITE,
  output RAM1_nOE,
  output RAM1_nWE,
  output RAM2_nWE,
  output RAM2_nOE,
  output ROM_nOE
);

  wire and_2_out, nor_1_out, nor_2_out, not_1_out, not_2_out, not_3_out, not_4_out, not_5_out, not_6_out,
       not_10_out, or_1_out, or_2_out, pulldown_1_out;

  PullDown pulldown_1 (.out(pulldown_1_out));
  _74138 A1_A3 (
    .pin1(A1), .pin2(A2), .pin3(A3), .pin4(AS), .pin5(pulldown_1_out), .pin6(1'b1), .pin7(nQ7), .pin8(1'b0),
    .pin9(nQ6), .pin10(nQ5), .pin11(nQ4), .pin12(nQ3), .pin13(nQ2), .pin14(nQ1), .pin15(nQ0), .pin16(1'b1));
  _74138 A4_A6 (
    .pin1(A4), .pin2(A5), .pin3(A6), .pin4(AS), .pin5(pulldown_1_out), .pin6(1'b1), .pin7(nQ7_2),
    .pin8(1'b0), .pin9(nQ6_2), .pin10(nQ5_2), .pin11(nQ4_2), .pin12(nQ3_2), .pin13(nQ2_2), .pin14(nQ1_2),
    .pin15(nQ0_2), .pin16(1'b1));
  _74138 A11_A13 (
    .pin1(A11), .pin2(A12), .pin3(A13), .pin4(AS), .pin5(pulldown_1_out), .pin6(1'b1), .pin7(nQ7_3),
    .pin8(1'b0), .pin9(nQ6_3), .pin10(nQ5_3), .pin11(nQ4_3), .pin12(nQ3_3), .pin13(nQ2_3), .pin14(nQ1_3),
    .pin15(nQ0_3), .pin16(1'b1));
  not not_1 (not_1_out, nQ0_3);
  not not_2 (not_2_out, nQ0_2);
  not not_3 (not_3_out, nQ1_3);
  not not_4 (not_4_out, nQ2_3);
  not not_5 (not_5_out, nQ3);
  nor nor_1 (nor_1_out, A7, A8, A9, A10);
  nor nor_2 (nor_2_out, A7, A9, A10);
  not not_6 (not_6_out, nQ3_3);
  and and_1 (ACIA_CS0, not_5_out, not_2_out, not_1_out, nor_1_out);
  and and_2 (and_2_out, A8, nor_2_out);
  not not_7 (ACIA_nCS2, ACIA_CS0);
  and and_3 (RTC_CS1, not_2_out, not_1_out, and_2_out);
  not not_8 (RAM1_nOE, AS);
  not not_9 (RTC_WRITE, R_nW);
  or or_1 (or_1_out, not_1_out, not_3_out);
  or or_2 (or_2_out, not_4_out, not_6_out);
  not not_10 (not_10_out, RTC_CS1);
  nand nand_1 (RAM1_nCS, not_10_out, or_1_out);
  nand nand_2 (RAM2_nCS, not_10_out, or_2_out);
  not not_11 (ROM_nCE, A13);

  assign ACIA_CS1 = ACIA_CS0;
  assign ACIA_E = ACIA_CS0;
  assign ACIA_R_nW = R_nW;
  assign ACIA_RS = A0;
  assign RAM1_nWE = R_nW;
  assign RAM2_nOE = RAM1_nOE;
  assign RAM2_nWE = R_nW;
  assign ROM_nOE = RAM1_nOE;
  assign RTC_ADDRESS_WRITE = AS;
  assign RTC_CS2 = RTC_CS1;
  assign RTC_READ = R_nW;
endmodule
