// Digital circuit New_Address_Decode.dig as structural Verilog
module New_Address_Decode (
  input  A0,
  input  A1,
  input  A2,
  input  A3,
  input  A4,
  input  A5,
  input  A6,
  input  A7,
  input  A8,
  input  A9,
  input  A10,
  input  A11,
  input  A12,
  input  R_nW,
  input  AS,
  output RAM_2_nCE,
  output nQ4,
  output nQ5,
  output nQ6,
  output nQ7,
  output ROM_nCE,
  output RTC_nCS,
  output RAM_1_nCS,
  output ACIA_nCS
);

  wire and_1_out, and_2_out, and_3_out, and_4_out, and_5_out, and_7_out, and_8_out, and_9_out, and_10_out,
       and_11_out, and_12_out, and_13_out, and_14_out, MX1_pin12, MX1_pin13, MX1_pin15, MX2_pin7, MX2_pin9,
       MX2_pin10, MX2_pin11, MX2_pin12, MX2_pin13, MX2_pin14, MX2_pin15, nor_1_out, nor_2_out, not_1_out,
       not_2_out, not_3_out, not_4_out, not_5_out, or_1_out, xor_1_out;

  nor nor_1 (nor_1_out, A4, A5);
  nor nor_2 (nor_2_out, A6, A7);
  _74138 MX1 (
    .pin1(A11), .pin2(A12), .pin3(1'b0), .pin4(1'b0), .pin5(1'b0), .pin6(AS), .pin7(nQ7), .pin8(1'b0),
    .pin9(nQ6), .pin10(nQ5), .pin11(nQ4), .pin12(MX1_pin12), .pin13(MX1_pin13), .pin14(RAM_2_nCE),
    .pin15(MX1_pin15), .pin16(1'b1));
  and and_1 (and_1_out, A2, not_1_out);
  not not_1 (not_1_out, A3);
  and and_2 (and_2_out, nor_1_out, nor_2_out);
  and and_3 (and_3_out, A1, and_1_out);
  not not_2 (not_2_out, A2);
  _74138 MX2 (
    .pin1(A8), .pin2(A9), .pin3(A10), .pin4(MX1_pin15), .pin5(MX1_pin15), .pin6(AS), .pin7(MX2_pin7),
    .pin8(1'b0), .pin9(MX2_pin9), .pin10(MX2_pin10), .pin11(MX2_pin11), .pin12(MX2_pin12), .pin13(MX2_pin13),
    .pin14(MX2_pin14), .pin15(MX2_pin15), .pin16(1'b1));
  and and_4 (and_4_out, A1, not_2_out);
  and and_5 (and_5_out, A2, A3);
  and and_6 (ROM_nCE, MX1_pin13, MX1_pin12);
  or or_1 (or_1_out, and_4_out, and_5_out);
  and and_7 (and_7_out, MX2_pin13, MX2_pin12);
  and and_8 (and_8_out, or_1_out, and_2_out);
  and and_9 (and_9_out, MX2_pin11, MX2_pin10);
  and and_10 (and_10_out, MX2_pin9, MX2_pin7);
  and and_11 (and_11_out, and_7_out, and_9_out);
  not not_3 (not_3_out, MX2_pin15);
  not not_4 (not_4_out, MX2_pin14);
  and and_12 (and_12_out, and_11_out, and_10_out);
  nand nand_1 (RTC_nCS, and_2_out, not_4_out);
  nand nand_2 (ACIA_nCS, and_3_out, not_3_out);
  and and_13 (and_13_out, and_8_out, not_3_out);
  xor xor_1 (xor_1_out, RTC_nCS, not_4_out);
  and and_14 (and_14_out, xor_1_out, and_12_out);
  not not_5 (not_5_out, and_13_out);
  and and_15 (RAM_1_nCS, not_5_out, and_14_out);

  // Notes on the sheet:
  //   R_nW: Read High, Write Low
  //   AS: Address Select
  //   RAM_2_nCE: RAM 2 ~CE
endmodule
